# Fritzing sketch Sketch (saved by Fritzing 0.9.2b)
breadboards: 1

parts:
  Raspberry_Pi1 = Raspberry Pi 2
  IC1 = MCP3008 8-channel 10-bit ADC [part_number=MCP3008]
  SONAR1 = Maxbotix MaxSonar Ultrasonic Sensor (Hi-Res)

nets:
  N1: Raspberry_Pi1.GPIO10, IC1.no_name_yet#11
  N2: Raspberry_Pi1.GPIO9, IC1.no_name_yet#12
  N3: Raspberry_Pi1.GPIO11, IC1.no_name_yet#13
  N4: Raspberry_Pi1.GPIO8, IC1.no_name_yet#10
  5V: Raspberry_Pi1.5V, IC1.no_name_yet#15, IC1.no_name_yet#16, SONAR1.+5V
  N5: IC1.no_name_yet#1, SONAR1.AN
  N6: IC1.no_name_yet#9, IC1.no_name_yet#14, SONAR1.GND

custom parts:
  Maxbotix MaxSonar Ultrasonic Sensor (Hi-Res): Maxbotix MaxSonar Hi-Resolution Ultrasonic Sensor HRLV-EZ0, HRLV-EZ1, HRLV-EZ2, HRLV-EZ3, HRLV-EZ4
